# Fritzing sketch test_circuit (saved by Fritzing 0.9.3b)
breadboards: 1

parts:
  M1 = STM32407VG Discovery
  C1 = Capacitor Polarized [package=cpol-radial-100uf-25v]
  C2 = Capacitor Polarized [package=cpol-radial-100uf-25v]  # not connected
  Part1 = USB converter CP2102
  U4 = ESP8266 WiFi Module [part_number=ESP8266]

nets:
  GND: M1.GND0, M1.GND-24, M1.GND-50, M1.GND-99, C1.-, Part1.GND, U4.GND
  N1: M1.PE15, U4.TXD
  N2: M1.PB10, U4.RXD
  N3: M1.PD5, Part1.RXI
  N4: M1.PD6, Part1.TXO
  N5: C1.+, U4.CH_PD

notes:
  uart2-PC
  uart3-ESP-01

custom parts:
  STM32407VG Discovery: The STM32F4DISCOVERY Discovery kit allows users to easily develop applications with the STM32F407VG high performance microcontroller with the ARM® Cortex®-M4 32-bit core. It includes everything required either for beginners or for experienced users to get quickly started.Based on STM32F407VG, it includes an ST-LINK/V2 or ST-LINK/V2-A embedded debug tool, two ST-MEMS digital accelerometers, a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
  ESP8266 WiFi Module: Generic WiFi Module based on the ESP8266 with onboard PCB antenna and UART communications
